// Logisim project drisc.circ as structural Verilog: 17 circuits, main circuit main
module main (
);

  wire Addr_ALU_Use_PC, Alu_Read, ALU_Use_PC, Call_Interrupt, Cl0ck, Data_IO_Read, Data_IO_Store,
       Enable_Interrupts, io_controller_1_data_2bytes, io_controller_1_data_4bytes,
       io_controller_1_read_keyboard, io_controller_1_read_os_ram, io_controller_1_readram,
       io_controller_1_write_os_ram, io_controller_1_write_video, io_controller_1_writeram, Is_Load_Store,
       keyboard_1_avail, Load_Upper_Immediate, not_1_out, P1_out, P2_out, P3_out, PadRead, PadWrite, PC_Jump,
       PC_Read_Next, PC_Use_Offset, PC_Write_Next, Phase1, Phase1n, Phase1s, Phase2, Phase2i, Phase2n,
       Phase2s, Phase3, Phase3i, Phase3n, Phase3s, por_1_out, por_2_out, por_3_out, por_4_out, por_5_out,
       por_6_out, por_7_out, Register_File_Write, register_history_generator_1_out_clock, Shifter_C_Out,
       Shifter_L_In, Shifter_L_Out, Use_Immediate;
  wire [1:0] Data_Offset;
  wire [2:0] Funct3;
  wire [3:0] alu_1_cnzv;
  wire [4:0] OP_Function;
  wire [7:0] io_controller_1_rom_address_out_8bit, keyboard_1_data;
  wire [14:0] Register_Addresses;
  wire [15:0] register_history_generator_1_out_value, shift_register_1_q0, shift_register_1_q1,
       shift_register_1_q2, shift_register_1_q3, shift_register_1_q4, shift_register_1_q5,
       shift_register_1_q6, shift_register_1_q7, shift_register_1_q8, shift_register_1_q9,
       shift_register_1_q10, shift_register_1_q11, shift_register_1_q12, shift_register_1_q13,
       shift_register_1_q14, shift_register_1_q15, shift_register_1_q16, shift_register_1_q17,
       shift_register_1_q18, shift_register_1_q19, shift_register_1_q20, shift_register_1_q21,
       shift_register_1_q22, shift_register_1_q23, shift_register_1_q24, shift_register_1_q25,
       shift_register_1_q26, shift_register_1_q27, shift_register_1_q28, shift_register_1_q29,
       shift_register_1_q30, shift_register_1_q31, shift_register_1_q32, shift_register_1_q33,
       shift_register_1_q34, shift_register_1_q35, shift_register_1_q36, shift_register_1_q37,
       shift_register_1_q38, shift_register_1_q39, shift_register_1_q40, shift_register_1_q41,
       shift_register_1_q42, shift_register_1_q43, shift_register_1_q44, shift_register_1_q45,
       shift_register_1_q46, shift_register_1_q47, shift_register_1_q48, shift_register_1_q49,
       shift_register_1_q50, shift_register_1_q51, shift_register_1_q52, shift_register_1_q53,
       shift_register_1_q54, shift_register_1_q55, shift_register_1_q56, shift_register_1_q57,
       shift_register_1_q58, shift_register_1_q59, shift_register_1_q60, shift_register_1_q61,
       shift_register_1_q62, shift_register_1_q63;
  wire [23:0] io_controller_1_address_out_24bit;
  wire [31:0] address_alu_1_result, alu_1_result, buffer_1_out, controlled_buffer_1_out,
       data_input_output_1_pbus_out, Immediate, io_controller_1_addressdebug, program_counter_1_c_bus_out,
       program_counter_1_p_bus_out, program_counter_1_program_counter_out, register_1_q,
       register_file_1_a_bus_out, register_file_1_b_bus_out, shifter_circuit_1_c_bus_out;

  // Probe on Register_Addresses[4:0]
  // Probe on Register_Addresses[9:5]
  // Probe on Register_Addresses[14:10]
  POR #(.porsize(2)) por_1 (.out(por_1_out));
  Register_File register_file_1 (
    .C_Bus_In(buffer_1_out), .Addresses_In(Register_Addresses), .Read(Phase1n), .Write(Register_File_Write),
    .Clock(Cl0ck), .Reset(por_1_out), .A_Bus_Out(register_file_1_a_bus_out),
    .B_Bus_Out(register_file_1_b_bus_out));
  // Probe on register_file_1_a_bus_out
  // Probe on register_file_1_b_bus_out
  // Probe on buffer_1_out
  // Probe on Immediate
  Register #(.trigger("falling"), .width(32)) register_1 (
    .D(register_file_1_b_bus_out), .en(Phase1n), .Q(register_1_q), .clk(Cl0ck));  // open: clr
  // Probe on controlled_buffer_1_out
  assign controlled_buffer_1_out = Data_IO_Store ? register_1_q : 32'bz;  // Controlled_Buffer controlled_buffer_1
  // Probe on data_input_output_1_pbus_out
  POR #(.porsize(2)) por_2 (.out(por_2_out));
  Data_Input_Output data_input_output_1 (
    .Data_Offset(Data_Offset), .Data_Size(Funct3[1:0]), .Read_To_L(Data_IO_Read),
    .IO_Bus_In(controlled_buffer_1_out), .Write_From_L(Data_IO_Store),
    .PBus_In(data_input_output_1_pbus_out), .Read_To_P(Data_IO_Store), .Write_From_P(Phase1s), .Clock(Cl0ck),
    .Unsigned_Data(Funct3[2]), .IO_Bus_Out(controlled_buffer_1_out), .PBus_Out(data_input_output_1_pbus_out));
  Shifter_Circuit shifter_circuit_1 (
    .Enable_C_Out(Shifter_C_Out), .Byte_Control_In(Data_Offset), .Clock(Cl0ck),
    .Select_Byte_Control(Is_Load_Store), .Select_Immediate(Use_Immediate),
    .B_Bus_In(register_file_1_b_bus_out), .Immediate_In(Immediate), .A_Bus_In(register_file_1_a_bus_out),
    .Write(Phase1), .LBus_In(controlled_buffer_1_out), .Enable_L_In(Shifter_L_In),
    .Operation_Select(OP_Function), .Calculate(Phase2), .C_Bus_Out(shifter_circuit_1_c_bus_out));
  // Probe on shifter_circuit_1_c_bus_out
  assign buffer_1_out = shifter_circuit_1_c_bus_out;  // Buffer buffer_1, 32 bits wide
  assign buffer_1_out = Load_Upper_Immediate ? Immediate : 32'bz;  // Controlled_Buffer controlled_buffer_2
  Register_History_Generator register_history_generator_1 (
    .Current_Value(buffer_1_out), .Current_Address(Register_Addresses[4:0]), .Target_Address(5'b00001),
    .Write_Signal(Register_File_Write), .Reset(por_2_out), .Clock(Cl0ck),
    .Out_Clock(register_history_generator_1_out_clock), .Out_Value(register_history_generator_1_out_value));
  Shift_Register #(.length(64), .width(16)) shift_register_1 (
    .in(register_history_generator_1_out_value), .clk(register_history_generator_1_out_clock),
    .clr(por_3_out), .q0(shift_register_1_q0), .q1(shift_register_1_q1), .q2(shift_register_1_q2),
    .q3(shift_register_1_q3), .q4(shift_register_1_q4), .q5(shift_register_1_q5), .q6(shift_register_1_q6),
    .q7(shift_register_1_q7), .q8(shift_register_1_q8), .q9(shift_register_1_q9), .q10(shift_register_1_q10),
    .q11(shift_register_1_q11), .q12(shift_register_1_q12), .q13(shift_register_1_q13),
    .q14(shift_register_1_q14), .q15(shift_register_1_q15), .q16(shift_register_1_q16),
    .q17(shift_register_1_q17), .q18(shift_register_1_q18), .q19(shift_register_1_q19),
    .q20(shift_register_1_q20), .q21(shift_register_1_q21), .q22(shift_register_1_q22),
    .q23(shift_register_1_q23), .q24(shift_register_1_q24), .q25(shift_register_1_q25),
    .q26(shift_register_1_q26), .q27(shift_register_1_q27), .q28(shift_register_1_q28),
    .q29(shift_register_1_q29), .q30(shift_register_1_q30), .q31(shift_register_1_q31),
    .q32(shift_register_1_q32), .q33(shift_register_1_q33), .q34(shift_register_1_q34),
    .q35(shift_register_1_q35), .q36(shift_register_1_q36), .q37(shift_register_1_q37),
    .q38(shift_register_1_q38), .q39(shift_register_1_q39), .q40(shift_register_1_q40),
    .q41(shift_register_1_q41), .q42(shift_register_1_q42), .q43(shift_register_1_q43),
    .q44(shift_register_1_q44), .q45(shift_register_1_q45), .q46(shift_register_1_q46),
    .q47(shift_register_1_q47), .q48(shift_register_1_q48), .q49(shift_register_1_q49),
    .q50(shift_register_1_q50), .q51(shift_register_1_q51), .q52(shift_register_1_q52),
    .q53(shift_register_1_q53), .q54(shift_register_1_q54), .q55(shift_register_1_q55),
    .q56(shift_register_1_q56), .q57(shift_register_1_q57), .q58(shift_register_1_q58),
    .q59(shift_register_1_q59), .q60(shift_register_1_q60), .q61(shift_register_1_q61),
    .q62(shift_register_1_q62), .q63(shift_register_1_q63));  // open: shift, out, load, d0, d1, d2, d3, d4, d5, d6, d7, d8, d9, d10, d11, d12, d13, d14, d15, d16, d17, d18, d19, d20, d21, d22, d23, d24, d25, d26, d27, d28, d29, d30, d31, d32, d33, d34, d35, d36, d37, d38, d39, d40, d41, d42, d43, d44, d45, d46, d47, d48, d49, d50, d51, d52, d53, d54, d55, d56, d57, d58, d59, d60, d61, d62, d63
  POR #(.porsize(2)) por_3 (.out(por_3_out));
  DotMatrix #(.matrixcols(64), .matrixrows(16)) dotmatrix_1 (
    .col0(shift_register_1_q0), .col1(shift_register_1_q1), .col2(shift_register_1_q2),
    .col3(shift_register_1_q3), .col4(shift_register_1_q4), .col5(shift_register_1_q5),
    .col6(shift_register_1_q6), .col7(shift_register_1_q7), .col8(shift_register_1_q8),
    .col9(shift_register_1_q9), .col10(shift_register_1_q10), .col11(shift_register_1_q11),
    .col12(shift_register_1_q12), .col13(shift_register_1_q13), .col14(shift_register_1_q14),
    .col15(shift_register_1_q15), .col16(shift_register_1_q16), .col17(shift_register_1_q17),
    .col18(shift_register_1_q18), .col19(shift_register_1_q19), .col20(shift_register_1_q20),
    .col21(shift_register_1_q21), .col22(shift_register_1_q22), .col23(shift_register_1_q23),
    .col24(shift_register_1_q24), .col25(shift_register_1_q25), .col26(shift_register_1_q26),
    .col27(shift_register_1_q27), .col28(shift_register_1_q28), .col29(shift_register_1_q29),
    .col30(shift_register_1_q30), .col31(shift_register_1_q31), .col32(shift_register_1_q32),
    .col33(shift_register_1_q33), .col34(shift_register_1_q34), .col35(shift_register_1_q35),
    .col36(shift_register_1_q36), .col37(shift_register_1_q37), .col38(shift_register_1_q38),
    .col39(shift_register_1_q39), .col40(shift_register_1_q40), .col41(shift_register_1_q41),
    .col42(shift_register_1_q42), .col43(shift_register_1_q43), .col44(shift_register_1_q44),
    .col45(shift_register_1_q45), .col46(shift_register_1_q46), .col47(shift_register_1_q47),
    .col48(shift_register_1_q48), .col49(shift_register_1_q49), .col50(shift_register_1_q50),
    .col51(shift_register_1_q51), .col52(shift_register_1_q52), .col53(shift_register_1_q53),
    .col54(shift_register_1_q54), .col55(shift_register_1_q55), .col56(shift_register_1_q56),
    .col57(shift_register_1_q57), .col58(shift_register_1_q58), .col59(shift_register_1_q59),
    .col60(shift_register_1_q60), .col61(shift_register_1_q61), .col62(shift_register_1_q62),
    .col63(shift_register_1_q63));
  Clock MainClock (.out(Cl0ck));
  POR #(.PorHighDuration(1), .porsize(2)) por_4 (.out(por_4_out));
  Clock #(.highDuration(2), .lowDuration(4), .phaseOffset(4)) P1 (.out(P1_out));
  Clock #(.highDuration(2), .lowDuration(4), .phaseOffset(2)) P2 (.out(P2_out));
  // Probe on alu_1_cnzv
  ALU alu_1 (
    .Calculate(Phase2), .Read(Alu_Read), .Clock(Cl0ck), .Use_PC(ALU_Use_PC), .Use_Immediate(Use_Immediate),
    .Source1(register_file_1_a_bus_out), .Program_Counter_In(program_counter_1_program_counter_out),
    .Source2(register_file_1_b_bus_out), .Immediate(Immediate), .Write(Phase1), .Operation(OP_Function),
    .CNZV(alu_1_cnzv), .Result(alu_1_result));
  // Probe on alu_1_result
  assign buffer_1_out = alu_1_result;  // Buffer buffer_2, 32 bits wide
  Clock #(.highDuration(2), .lowDuration(4)) P3 (.out(P3_out));
  Clock_Circuit clock_circuit_1 (
    .Phase3_in(P3_out), .Load_Store_Instruction(Is_Load_Store),
    .Return_Interrupt_Instruction(Enable_Interrupts), .Interrupt(Call_Interrupt), .Reset(por_4_out),
    .Phase1_In(P1_out), .Phase2_In(P2_out), .Phase3(Phase3), .Phase3i(Phase3i), .Phase3n(Phase3n),
    .Phase3s(Phase3s), .Phase1(Phase1), .Phase1n(Phase1n), .Phase1s(Phase1s), .Phase2(Phase2),
    .Phase2i(Phase2i), .Phase2n(Phase2n), .Phase2s(Phase2s));  // open: Window_Overflow
  POR #(.PorHighDuration(1), .porsize(2)) por_5 (.out(por_5_out));
  Address_ALU address_alu_1 (
    .Clock(Cl0ck), .Use_PC(Addr_ALU_Use_PC), .Source1(register_file_1_a_bus_out),
    .Program_Counter_In(program_counter_1_program_counter_out), .Immediate(Immediate), .Write(Phase1),
    .Calculate(Phase2), .Result(address_alu_1_result));
  // Probe on {Phase3i, Phase2i, Phase3s, Phase2s, Phase1s, Phase3n, Phase2n, Phase1n}
  Operation_Controller operation_controller_1 (
    .P_Bus_In(data_input_output_1_pbus_out), .CNZV(alu_1_cnzv), .Clock(Cl0ck), .Reset(por_5_out),
    .Phase1n(Phase1n), .Phase2n(Phase2n), .Phase3n(Phase3n), .Phase1s(Phase1s), .Phase2s(Phase2s),
    .Phase3s(Phase3s), .Phase2i(Phase2i), .Phase3i(Phase3i), .Immediate(Immediate),
    .Register_File_Write(Register_File_Write), .PC_Write_Next(PC_Write_Next), .PC_Use_Offset(PC_Use_Offset),
    .PC_Read_Next(PC_Read_Next), .PC_Jump(PC_Jump), .Alu_Read(Alu_Read), .Data_IO_Store(Data_IO_Store),
    .Data_IO_Read(Data_IO_Read), .OP_Function(OP_Function), .Address_ALU_Use_PC(Addr_ALU_Use_PC),
    .Shifter_Read_C(Shifter_C_Out), .Load_Store(Is_Load_Store), .PAD_Write(PadWrite), .PAD_Read(PadRead),
    .Shifter_Write_L(Shifter_L_In), .Shifter_Read_L(Shifter_L_Out),
    .Load_Upper_Immediate(Load_Upper_Immediate), .ALU_Use_PC(ALU_Use_PC), .Use_Immediate(Use_Immediate),
    .Register_Adresses(Register_Addresses), .Funct3(Funct3));
  POR #(.porsize(2)) por_6 (.out(por_6_out));
  Program_Counter program_counter_1 (
    .Enable_Last_Out(1'b0), .D_Bus_In(address_alu_1_result), .Jump(PC_Jump), .Reset(por_6_out),
    .Clock(Cl0ck), .Load_Interrupt_Vector(Phase3i), .Use_Offset(PC_Use_Offset), .Write(PC_Write_Next),
    .Next_P_Out(Phase1n), .D_Bus_To_P(Phase3s), .Enable_Next_Out(PC_Read_Next), .Byte_Offset(Data_Offset),
    .P_Bus_Out(program_counter_1_p_bus_out), .Program_Counter_Out(program_counter_1_program_counter_out),
    .C_Bus_Out(program_counter_1_c_bus_out));
  // Probe on program_counter_1_c_bus_out
  assign buffer_1_out = program_counter_1_c_bus_out;  // Buffer buffer_3, 32 bits wide
  assign data_input_output_1_pbus_out = program_counter_1_p_bus_out;  // Buffer buffer_4, 32 bits wide
  // Probe on program_counter_1_p_bus_out
  POR #(.PorHighDuration(1), .porsize(2)) por_7 (.out(por_7_out));
  // Probe on io_controller_1_addressdebug
  IO_Controller io_controller_1 (
    .Phase1n(Phase1n), .Phase3s(Phase3s), .Phase3i(Phase3i), .Address_In(data_input_output_1_pbus_out),
    .Clock(Cl0ck), .Reset(por_7_out), .Keyboard_Address(32'h1ffe), .Video_Address({32{1'b1}}),
    .Write(PadWrite), .Data_Size(Funct3[1:0]), .Read(PadRead), .WriteRam(io_controller_1_writeram),
    .Write_OS_Ram(io_controller_1_write_os_ram), .AddressDebug(io_controller_1_addressdebug),
    .Read_Keyboard(io_controller_1_read_keyboard), .Write_Video(io_controller_1_write_video),
    .Read_OS_Ram(io_controller_1_read_os_ram), .Data_2Bytes(io_controller_1_data_2bytes),
    .Data_4Bytes(io_controller_1_data_4bytes), .ReadRam(io_controller_1_readram),
    .Address_Out_24Bit(io_controller_1_address_out_24bit),
    .Rom_Address_Out_8Bit(io_controller_1_rom_address_out_8bit));
  // RAM #(.addrWidth(24), .databus("bidir"), .enables("line"), .line("quad"), .misaligned("true"), .trigger("high"), .\type ("nonvolatile")) ram_1: pin names not known; wires that end beside it: io_controller_1_address_out_24bit, io_controller_1_writeram, io_controller_1_readram, 1'b1, io_controller_1_data_2bytes, io_controller_1_data_4bytes, Cl0ck
  ROM #(.dataWidth(32)) rom_1 (.addr(io_controller_1_rom_address_out_8bit), .data(data_input_output_1_pbus_out));
  // RAM #(.addrWidth(24), .clearpin("true"), .databus("bidir"), .enables("line"), .line("quad"), .misaligned("true"), .trigger("high"), .\type ("nonvolatile")) ram_2: pin names not known; wires that end beside it: io_controller_1_address_out_24bit, io_controller_1_write_os_ram, io_controller_1_read_os_ram, 1'b1, io_controller_1_data_2bytes, io_controller_1_data_4bytes, Cl0ck
  Button R ();  // open: out
  Keyboard keyboard_1 (
    .clk(io_controller_1_read_keyboard), .re(1'b1), .avail(keyboard_1_avail), .data(keyboard_1_data[6:0]));  // open: clr
  assign data_input_output_1_pbus_out = io_controller_1_read_keyboard ? {{24{1'b0}}, keyboard_1_data} : 32'bz;  // Controlled_Buffer controlled_buffer_3
  not not_1 (not_1_out, Cl0ck);
  not not_2 (keyboard_1_data[7], keyboard_1_avail);
  // RGB_Video #(.cursor("No Cursor"), .height(64), .reset("Synchronous"), .scale(6), .width(64)) rgb_video_1: pin names not known; wires that end beside it: data_input_output_1_pbus_out[31], not_1_out, io_controller_1_write_video, data_input_output_1_pbus_out[27:22], data_input_output_1_pbus_out[21:16], data_input_output_1_pbus_out[15:0]

  // Notes on the sheet:
  //   Program Counter
  //   Processor < > Input Output Devices
  //   contents of rom_1 (hex, n*v repeats v):
  //   d0c00000 25b80000 b1b5a001 21b5a01f e1ae0000 51a56000 519e6000 e1940000 a19cc012 150da0ac b1000000
  //   71d52004 71dd2008 71e5200c 71f52010 71ed2014 71fd2018 b1dd2000 19502004 7182e01c 718ae020 7192e024
  //   719ae028 71a2e02c 71aae030 71b2e034 71bae038 71c2e03c 71cae040 b152a034 c100000a b1a52040 71a56000
  //   b1a5e010 81a52070 b1ade080 81ad6380 81bdfc0f 91bdc014 91bdc015 3505c000 147e4000 c87e0000 b1fbe000
  //   b1f3a000 b1eb6000 b1e32000 b1dae000 b1d2a000 b1552000 d1800000 b1842010 c1000010 b1fbe000 b1f3a000
  //   b1eb6000 b1e32000 b1dae000 b15ea000 b1d2a000 d1780000 b17be010 c100000f 51cee000 51c6fffc 51befff8
  //   51b6fff4 51aefff0 51a6ffec 519effe8 5196ffe4 518effe0 5186ffdc 517effd8 5176ffd4 516effd0 5166ffcc
  //   515effc8 5156ffc4 19002004 b17fe000 b177a000 b16f6000 b1672000 b15ee000 b156a000 19002004 b17fe000
  //   b177a000 b16f6000 b1672000 b15ee000 b156a000 a1a52040 71a56000 a1a5e010 81a52070 b1ade080 81ad6380
  //   81bdfc0f 91bdc014 91bdc015 3505c000 147e4000 c87e0000
  //   Interrupt Routines ROM
  //   OS RAM
endmodule

module Clock_Circuit (
  input  Interrupt,
  input  Reset,
  input  Phase1_In,
  input  Phase2_In,
  input  Phase3_in,
  input  Load_Store_Instruction,
  input  Window_Overflow,
  input  Return_Interrupt_Instruction,
  output Phase2n,
  output Phase1,
  output Phase1s,
  output Phase2,
  output Phase3,
  output Phase3n,
  output Phase2s,
  output Phase1n,
  output Phase2i,
  output Phase3i,
  output Phase3s
);

  wire and_1_out, and_2_out, and_8_out, and_12_out, Interrupt_Enable_q, Interruption_q, not_1_out, not_2_out,
       not_3_out, or_1_out, or_2_out, or_3_out, SecondaryA_q, SecondaryB_q;

  and and_1 (and_1_out, Return_Interrupt_Instruction, Phase3n);
  or or_1 (or_1_out, Interrupt, Window_Overflow);
  Register #(.trigger("high"), .width(1)) Interrupt_Enable (
    .D(and_1_out), .en(and_1_out), .clk(1'b1), .Q(Interrupt_Enable_q), .clr(or_2_out));
  or or_2 (or_2_out, Phase2i, Reset);
  and and_2 (and_2_out, or_1_out, Interrupt_Enable_q);
  or or_3 (or_3_out, Reset, and_2_out);
  and and_3 (Phase1n, not_2_out, Phase1_In);
  and and_4 (Phase1s, SecondaryA_q, Phase1_In);
  Register #(.trigger("high"), .width(1)) Interruption (
    .D(or_3_out), .en(Phase1_In), .clk(Phase1_In), .Q(Interruption_q), .clr(Reset));
  not not_1 (not_1_out, Interruption_q);
  and and_5 (Phase2i, Interruption_q, Phase2_In);
  and and_6 (Phase2n, not_3_out, not_1_out, Phase2_In);
  and and_7 (Phase2s, SecondaryB_q, not_1_out, Phase2_In);
  Register #(.trigger("high"), .width(1)) SecondaryA (
    .D(and_8_out), .en(Phase2_In), .clk(Phase2_In), .Q(SecondaryA_q), .clr(Reset));
  and and_8 (and_8_out, Load_Store_Instruction, not_3_out);
  not not_2 (not_2_out, SecondaryA_q);
  and and_9 (Phase3i, Interruption_q, Phase3_in);
  and and_10 (Phase3n, not_2_out, not_1_out, Phase3_in);
  and and_11 (Phase3s, SecondaryA_q, not_1_out, Phase3_in);
  Register #(.trigger("high"), .width(1)) SecondaryB (
    .D(and_12_out), .en(Phase3_in), .clk(Phase3_in), .Q(SecondaryB_q), .clr(Reset));
  and and_12 (and_12_out, not_1_out, SecondaryA_q);
  not not_3 (not_3_out, SecondaryB_q);

  assign Phase1 = Phase1_In;
  assign Phase2 = Phase2_In;
  assign Phase3 = Phase3_in;
endmodule

module ALU (
  input  [4:0] Operation,
  input  Write,
  input  Calculate,
  input  Read,
  input  Use_PC,
  input  [31:0] Source1,
  input  [31:0] Program_Counter_In,
  input  Use_Immediate,
  input  [31:0] Source2,
  input  [31:0] Immediate,
  input  Clock,
  output [31:0] Result,
  output [3:0] CNZV
);

  wire adder_1_cout, comparator_1_lt, comparator_2_lt, multiplexer_5_out, not_1_out, subtractor_1_bout;
  wire [1:0] and_2_out;
  wire [30:0] Result_Reg_q;
  wire [31:0] adder_1_out, and_1_out, bit_extender_1_out, bit_extender_2_out, divider_1_out, divider_1_rem,
       divider_2_out, divider_2_rem, multiplexer_1_out, multiplexer_2_out, multiplexer_3_out,
       multiplexer_4_out, multiplier_1_cout, multiplier_1_out, multiplier_2_cout, or_1_out, Source_1_q,
       Source_2_q, subtractor_1_out, xor_1_out;

  not not_1 (not_1_out, Clock);
  Multiplexer #(.width(32)) multiplexer_1 (
    .in0(Source1), .in1(Program_Counter_In), .out(multiplexer_1_out), .sel(Use_PC));
  Multiplexer #(.width(32)) multiplexer_2 (
    .in0(Source2), .in1(Immediate), .out(multiplexer_2_out), .sel(Use_Immediate));
  Register #(.width(32)) Source_1 (.D(multiplexer_1_out), .en(Write), .clk(not_1_out), .Q(Source_1_q));  // open: clr
  Register #(.width(32)) Source_2 (.D(multiplexer_2_out), .en(Write), .clk(not_1_out), .Q(Source_2_q));  // open: clr
  assign or_1_out = Source_1_q | Source_2_q;  // OR_Gate or_1, 32 bits wide
  assign and_1_out = Source_1_q & Source_2_q;  // AND_Gate and_1, 32 bits wide
  Adder #(.width(32)) adder_1 (.a(Source_1_q), .b(Source_2_q), .out(adder_1_out), .cout(adder_1_cout));  // open: cin
  assign bit_extender_1_out = {{31{1'b0}}, comparator_1_lt};  // Bit_Extender bit_extender_1
  Comparator #(.width(32)) comparator_1 (.a(Source_1_q), .b(Source_2_q), .lt(comparator_1_lt));  // open: gt, eq
  assign bit_extender_2_out = {{31{1'b0}}, comparator_2_lt};  // Bit_Extender bit_extender_2
  Comparator #(.mode("unsigned"), .width(32)) comparator_2 (
    .a(Source_1_q), .b(Source_2_q), .lt(comparator_2_lt));  // open: gt, eq
  assign xor_1_out = Source_1_q ^ Source_2_q;  // XOR_Gate xor_1, 32 bits wide
  Multiplier #(.mode("twosComplement"), .width(32)) multiplier_1 (
    .a(Source_1_q), .b(Source_2_q), .out(multiplier_1_out), .cout(multiplier_1_cout));  // open: cin
  Multiplier #(.width(32)) multiplier_2 (.a(Source_1_q), .b(Source_2_q), .cout(multiplier_2_cout));  // open: out, cin
  Divider #(.mode("twosComplement"), .width(32)) divider_1 (
    .a(Source_1_q), .b(Source_2_q), .out(divider_1_out), .rem(divider_1_rem));  // open: upper
  Divider #(.width(32)) divider_2 (
    .a(Source_1_q), .b(Source_2_q), .out(divider_2_out), .rem(divider_2_rem));  // open: upper
  Subtractor #(.width(32)) subtractor_1 (
    .a(Source_1_q), .b(Source_2_q), .out(subtractor_1_out), .bout(subtractor_1_bout));  // open: bin
  assign and_2_out = Operation[4:3] & ~{2{Use_Immediate}};  // AND_Gate and_2, 2 bits wide
  Multiplexer #(.select(4), .width(32)) multiplexer_3 (
    .in0(adder_1_out), .in1({32{1'b0}}), .in2(bit_extender_1_out), .in3(bit_extender_2_out), .in4(xor_1_out),
    .in5({32{1'b0}}), .in6(or_1_out), .in7(and_1_out), .in8(multiplier_1_out), .in9(multiplier_1_cout),
    .in10({32{1'b0}}), .in11(multiplier_2_cout), .in12(divider_1_out), .in13(divider_2_out),
    .in14(divider_1_rem), .in15(divider_2_rem), .out(multiplexer_3_out), .sel({and_2_out[0], Operation[2:0]}));
  Multiplexer #(.width(32)) multiplexer_4 (
    .in0(multiplexer_3_out), .in1(subtractor_1_out), .out(multiplexer_4_out), .sel(and_2_out[1]));
  Multiplexer multiplexer_5 (.in0(adder_1_cout), .in1(subtractor_1_bout), .out(multiplexer_5_out), .sel(and_2_out[1]));
  Register #(.width(32)) Result_Reg (
    .D(multiplexer_4_out), .en(Calculate), .clk(not_1_out), .Q({CNZV[1], Result_Reg_q}));  // open: clr
  Register #(.width(1)) register_1 (.D(multiplexer_5_out), .en(Calculate), .clk(not_1_out), .Q(CNZV[0]));  // open: clr
  nor nor_1 (CNZV[2], Result_Reg_q[0], Result_Reg_q[1], Result_Reg_q[2], Result_Reg_q[3], Result_Reg_q[4], Result_Reg_q[5], Result_Reg_q[6], Result_Reg_q[7], Result_Reg_q[8], Result_Reg_q[9], Result_Reg_q[10], Result_Reg_q[11], Result_Reg_q[12], Result_Reg_q[13], Result_Reg_q[14], Result_Reg_q[15], Result_Reg_q[16], Result_Reg_q[17], Result_Reg_q[18], Result_Reg_q[19], Result_Reg_q[20], Result_Reg_q[21], Result_Reg_q[22], Result_Reg_q[23], Result_Reg_q[24], Result_Reg_q[25], Result_Reg_q[26], Result_Reg_q[27], Result_Reg_q[28], Result_Reg_q[29], Result_Reg_q[30], CNZV[1]);
  xor xor_2 (CNZV[3], CNZV[1], CNZV[0]);
  assign Result = Read ? {CNZV[1], Result_Reg_q} : 32'bz;  // Controlled_Buffer controlled_buffer_1

  // Notes on the sheet:
  //   Source1: initial=0xffffffff
  //   TODO: MULHSU
endmodule

module Program_Counter (
  input  Enable_Next_Out,
  input  Enable_Last_Out,
  input  Load_Interrupt_Vector,
  input  Write,
  input  Reset,
  input  Clock,
  input  Jump,
  input  Next_P_Out,
  input  [31:0] D_Bus_In,
  input  Use_Offset,
  input  D_Bus_To_P,
  output [31:0] C_Bus_Out,
  output [31:0] Program_Counter_Out,
  output [31:0] P_Bus_Out,
  output [1:0] Byte_Offset
);

  wire not_1_out, not_2_out;
  wire [1:0] and_1_out;
  wire [29:0] adder_1_out, controlled_buffer_1_out, multiplexer_1_out;
  wire [31:2] Last_q, Next_PC_q;

  Adder #(.width(30)) adder_1 (.a(Next_PC_q), .b(30'h1), .out(adder_1_out));  // open: cin, cout
  assign controlled_buffer_1_out = not_2_out ? multiplexer_1_out : 30'bz;  // Controlled_Buffer controlled_buffer_1
  Multiplexer #(.width(30)) multiplexer_1 (
    .in0(adder_1_out), .in1(30'h20000000), .out(multiplexer_1_out), .sel(Load_Interrupt_Vector));
  not not_1 (not_1_out, Clock);
  not not_2 (not_2_out, Jump);
  Register #(.width(30)) Next_PC (.D(controlled_buffer_1_out), .en(Write), .clk(not_1_out), .Q(Next_PC_q), .clr(Reset));
  assign controlled_buffer_1_out = Jump ? D_Bus_In[31:2] : 30'bz;  // Controlled_Buffer controlled_buffer_2
  assign and_1_out = D_Bus_In[1:0] & {2{Use_Offset}};  // AND_Gate and_1, 2 bits wide
  assign C_Bus_Out = Enable_Next_Out ? {Next_PC_q, 2'b00} : 32'bz;  // Controlled_Buffer controlled_buffer_3
  assign P_Bus_Out = Next_P_Out ? {Next_PC_q, 2'b00} : 32'bz;  // Controlled_Buffer controlled_buffer_4
  assign P_Bus_Out = D_Bus_To_P ? {D_Bus_In[31:2], and_1_out} : 32'bz;  // Controlled_Buffer controlled_buffer_5
  Register #(.width(2)) Byte_Offset_Reg (.D(D_Bus_In[1:0]), .en(D_Bus_To_P), .clk(Clock), .Q(Byte_Offset), .clr(Reset));
  Register #(.width(30)) Current (
    .D(Next_PC_q), .en(Write), .clk(not_1_out), .Q(Program_Counter_Out[31:2]), .clr(Reset));
  Register #(.width(30)) Last (.D(Program_Counter_Out[31:2]), .en(Write), .clk(not_1_out), .Q(Last_q), .clr(Reset));
  assign C_Bus_Out = Enable_Last_Out ? {Last_q, 2'b00} : 32'bz;  // Controlled_Buffer controlled_buffer_6

  assign Program_Counter_Out[1:0] = 2'b00;
endmodule

module Immediate_Register (
  input  [31:0] Pbus_In,
  input  Write_Enable,
  input  Clock,
  input  LoadHigh,
  output [4:0] Shift_Amount,
  output Immediate_Flag,
  output [31:0] Immediate_13bit,
  output [31:0] Immediate_19bit
);

  wire [18:5] Immediate_q;
  wire [31:0] bit_extender_2_out;

  Register #(.width(19)) Immediate (
    .D(Pbus_In[18:0]), .en(Write_Enable), .clk(Clock),
    .Q({Immediate_q[18:14], Immediate_Flag, Immediate_q[12:5], Shift_Amount}));  // open: clr
  assign Immediate_13bit = {{19{Immediate_q[12]}}, {Immediate_q[12:5], Shift_Amount}};  // Bit_Extender bit_extender_1
  assign bit_extender_2_out = {{13{Immediate_q[18]}}, {Immediate_q[18:14], Immediate_Flag, Immediate_q[12:5], Shift_Amount}};  // Bit_Extender bit_extender_2
  Multiplexer #(.width(32)) multiplexer_1 (
    .in0(bit_extender_2_out),
    .in1({Immediate_q[18:14], Immediate_Flag, Immediate_q[12:5], Shift_Amount, {13{1'b0}}}),
    .out(Immediate_19bit), .sel(LoadHigh));
endmodule

module Shifter_Circuit (
  input  Select_Byte_Control,
  input  Select_Immediate,
  input  [31:0] B_Bus_In,
  input  [31:0] Immediate_In,
  input  [1:0] Byte_Control_In,
  input  [4:0] Operation_Select,
  input  Enable_C_Out,
  input  Write,
  input  [31:0] A_Bus_In,
  input  [31:0] LBus_In,
  input  Enable_L_In,
  input  Calculate,
  input  Clock,
  output [31:0] C_Bus_Out
);

  wire not_1_out;
  wire [4:0] multiplexer_1_out, multiplexer_2_out, Shift_Amount_Latch_q;
  wire [31:0] multiplexer_3_out, multiplexer_4_out, Shift_In_Latch_q, Shift_Out_Latch_q, shifter_1_out,
       shifter_2_out, shifter_3_out;

  Multiplexer #(.width(5)) multiplexer_1 (
    .in0(B_Bus_In[4:0]), .in1(Immediate_In[4:0]), .out(multiplexer_1_out), .sel(Select_Immediate));
  Multiplexer #(.width(5)) multiplexer_2 (
    .in0(multiplexer_1_out), .in1({Byte_Control_In, 3'b000}), .out(multiplexer_2_out),
    .sel(Select_Byte_Control));
  not not_1 (not_1_out, Clock);
  Register #(.width(5)) Shift_Amount_Latch (
    .D(multiplexer_2_out), .en(Write), .clk(not_1_out), .Q(Shift_Amount_Latch_q));  // open: clr
  Register #(.width(32)) Shift_In_Latch (.D(A_Bus_In), .en(Write), .clk(not_1_out), .Q(Shift_In_Latch_q));  // open: clr
  Multiplexer #(.width(32)) multiplexer_3 (
    .in0(Shift_In_Latch_q), .in1(LBus_In), .out(multiplexer_3_out), .sel(Enable_L_In));
  Shifter #(.width(32)) shifter_1 (.in(multiplexer_3_out), .\dist (Shift_Amount_Latch_q), .out(shifter_1_out));
  Shifter #(.shift("lr"), .width(32)) shifter_2 (
    .in(multiplexer_3_out), .\dist (Shift_Amount_Latch_q), .out(shifter_2_out));
  Shifter #(.shift("ar"), .width(32)) shifter_3 (
    .in(multiplexer_3_out), .\dist (Shift_Amount_Latch_q), .out(shifter_3_out));
  Multiplexer #(.select(2), .width(32)) multiplexer_4 (
    .in0(shifter_1_out), .in1(shifter_2_out), .in2(shifter_3_out), .in3(shifter_3_out),
    .out(multiplexer_4_out), .sel({Operation_Select[4], Operation_Select[2]}));
  Register #(.width(32)) Shift_Out_Latch (
    .D(multiplexer_4_out), .en(Calculate), .clk(Clock), .Q(Shift_Out_Latch_q));  // open: clr
  assign C_Bus_Out = Enable_C_Out ? Shift_Out_Latch_q : 32'bz;  // Controlled_Buffer controlled_buffer_1
endmodule

module Data_Input_Output (
  input  Read_To_P,
  input  Write_From_P,
  input  [1:0] Data_Offset,
  input  Unsigned_Data,
  input  [1:0] Data_Size,
  input  Write_From_L,
  input  Read_To_L,
  input  [31:0] PBus_In,
  input  [31:0] IO_Bus_In,
  input  Clock,
  output [31:0] PBus_Out,
  output [31:0] IO_Bus_Out
);

  wire and_1_out, and_2_out, and_3_out, not_1_out, or_1_out;
  wire [2:0] byte_decoder_1_mux_enables;
  wire [7:0] bit_extender_1_out, bit_extender_2_out, bit_extender_3_out, multiplexer_1_out,
       multiplexer_2_out, multiplexer_3_out, multiplexer_4_out, multiplexer_5_out, multiplexer_6_out,
       multiplexer_7_out, register_1_q, register_2_q, register_3_q, register_4_q;
  wire [31:0] controlled_buffer_2_out, controlled_buffer_7_out;

  assign PBus_Out = Read_To_P ? controlled_buffer_2_out : 32'bz;  // Controlled_Buffer controlled_buffer_1
  assign controlled_buffer_2_out = Write_From_P ? PBus_In : 32'bz;  // Controlled_Buffer controlled_buffer_2
  assign controlled_buffer_2_out[7:0] = Read_To_P ? register_1_q : 8'bz;  // Controlled_Buffer controlled_buffer_3
  assign controlled_buffer_2_out[15:8] = Read_To_P ? register_2_q : 8'bz;  // Controlled_Buffer controlled_buffer_4
  assign controlled_buffer_2_out[23:16] = Read_To_P ? register_3_q : 8'bz;  // Controlled_Buffer controlled_buffer_5
  assign controlled_buffer_2_out[31:24] = Read_To_P ? register_4_q : 8'bz;  // Controlled_Buffer controlled_buffer_6
  Multiplexer #(.width(8)) multiplexer_1 (
    .in0(controlled_buffer_2_out[7:0]), .in1(controlled_buffer_7_out[7:0]), .out(multiplexer_1_out),
    .sel(Write_From_L));
  Multiplexer #(.width(8)) multiplexer_2 (
    .in0(controlled_buffer_2_out[15:8]), .in1(controlled_buffer_7_out[15:8]), .out(multiplexer_2_out),
    .sel(Write_From_L));
  Multiplexer #(.width(8)) multiplexer_3 (
    .in0(controlled_buffer_2_out[23:16]), .in1(controlled_buffer_7_out[23:16]), .out(multiplexer_3_out),
    .sel(Write_From_L));
  Multiplexer #(.width(8)) multiplexer_4 (
    .in0(controlled_buffer_2_out[31:24]), .in1(controlled_buffer_7_out[31:24]), .out(multiplexer_4_out),
    .sel(Write_From_L));
  or or_1 (or_1_out, Write_From_P, Write_From_L);
  Register register_1 (.D(multiplexer_1_out), .en(or_1_out), .clk(Clock), .Q(register_1_q));  // open: clr
  Register register_2 (.D(multiplexer_2_out), .en(or_1_out), .clk(Clock), .Q(register_2_q));  // open: clr
  Register register_3 (.D(multiplexer_3_out), .en(or_1_out), .clk(Clock), .Q(register_3_q));  // open: clr
  Register register_4 (.D(multiplexer_4_out), .en(or_1_out), .clk(Clock), .Q(register_4_q));  // open: clr
  not not_1 (not_1_out, Unsigned_Data);
  and and_1 (and_1_out, not_1_out, register_1_q[7]);
  and and_2 (and_2_out, not_1_out, multiplexer_5_out[7]);
  and and_3 (and_3_out, not_1_out, multiplexer_6_out[7]);
  assign bit_extender_1_out = {{7{and_1_out}}, and_1_out};  // Bit_Extender bit_extender_1
  Multiplexer #(.width(8)) multiplexer_5 (
    .in0(bit_extender_1_out), .in1(register_2_q), .out(multiplexer_5_out), .sel(byte_decoder_1_mux_enables[0]));
  assign bit_extender_2_out = {{7{and_2_out}}, and_2_out};  // Bit_Extender bit_extender_2
  Multiplexer #(.width(8)) multiplexer_6 (
    .in0(bit_extender_2_out), .in1(register_3_q), .out(multiplexer_6_out), .sel(byte_decoder_1_mux_enables[1]));
  assign bit_extender_3_out = {{7{and_3_out}}, and_3_out};  // Bit_Extender bit_extender_3
  Multiplexer #(.width(8)) multiplexer_7 (
    .in0(bit_extender_3_out), .in1(register_4_q), .out(multiplexer_7_out), .sel(byte_decoder_1_mux_enables[2]));
  Byte_Decoder byte_decoder_1 (
    .Data_Size(Data_Size), .Data_Offset(Data_Offset), .Mux_Enables(byte_decoder_1_mux_enables));
  assign controlled_buffer_7_out[7:0] = Read_To_L ? register_1_q : 8'bz;  // Controlled_Buffer controlled_buffer_7
  assign controlled_buffer_7_out[15:8] = Read_To_L ? multiplexer_5_out : 8'bz;  // Controlled_Buffer controlled_buffer_8
  assign controlled_buffer_7_out[23:16] = Read_To_L ? multiplexer_6_out : 8'bz;  // Controlled_Buffer controlled_buffer_9
  assign controlled_buffer_7_out[31:24] = Read_To_L ? multiplexer_7_out : 8'bz;  // Controlled_Buffer controlled_buffer_10
  assign IO_Bus_Out = Read_To_L ? controlled_buffer_7_out : 32'bz;  // Controlled_Buffer controlled_buffer_11
  assign controlled_buffer_7_out = Write_From_L ? IO_Bus_In : 32'bz;  // Controlled_Buffer controlled_buffer_12

  // Notes on the sheet:
  //   IO_Bus_In: initial=0xe3e3e3e3
  //   PBus_In: initial=0xf2f2f2f2
endmodule

module Register_File (
  input  [14:0] Addresses_In,
  input  [31:0] C_Bus_In,
  input  Read,
  input  Write,
  input  Clock,
  input  Reset,
  output [31:0] A_Bus_Out,
  output [31:0] B_Bus_Out
);

  Register_Bank register_bank_1 (
    .Address_A(Addresses_In[9:5]), .Address_B(Addresses_In[14:10]), .Read_Enable(Read), .Data_In(C_Bus_In),
    .Clock(Clock), .Address_C(Addresses_In[4:0]), .Write_Enable(Write), .Reset(Reset),
    .A_Data_Out(A_Bus_Out), .B_Data_Out(B_Bus_Out));
endmodule

module Register_Bank (
  input  Read_Enable,
  input  [4:0] Address_A,
  input  Reset,
  input  [31:0] Data_In,
  input  Clock,
  input  [4:0] Address_C,
  input  [4:0] Address_B,
  input  Write_Enable,
  output [31:0] A_Data_Out,
  output [31:0] B_Data_Out
);

  wire [31:0] decoder_1_out0, x1_q, x2_q, x3_q, x4_q, x5_q, x6_q, x7_q, x8_q, x9_q, x10_q, x11_q, x12_q,
       x13_q, x14_q, x15_q, x16_q, x17_q, x18_q, x19_q, x20_q, x21_q, x22_q, x23_q, x24_q, x25_q, x26_q,
       x27_q, x28_q, x29_q, x30_q, x31_q;

  Decoder #(.select(5)) decoder_1 (
    .out0(decoder_1_out0[0]), .out1(decoder_1_out0[1]), .out2(decoder_1_out0[2]), .out3(decoder_1_out0[3]),
    .out4(decoder_1_out0[4]), .out5(decoder_1_out0[5]), .out6(decoder_1_out0[6]), .out7(decoder_1_out0[7]),
    .out8(decoder_1_out0[8]), .out9(decoder_1_out0[9]), .out10(decoder_1_out0[10]),
    .out11(decoder_1_out0[11]), .out12(decoder_1_out0[12]), .out13(decoder_1_out0[13]),
    .out14(decoder_1_out0[14]), .out15(decoder_1_out0[15]), .out16(decoder_1_out0[16]),
    .out17(decoder_1_out0[17]), .out18(decoder_1_out0[18]), .out19(decoder_1_out0[19]),
    .out20(decoder_1_out0[20]), .out21(decoder_1_out0[21]), .out22(decoder_1_out0[22]),
    .out23(decoder_1_out0[23]), .out24(decoder_1_out0[24]), .out25(decoder_1_out0[25]),
    .out26(decoder_1_out0[26]), .out27(decoder_1_out0[27]), .out28(decoder_1_out0[28]),
    .out29(decoder_1_out0[29]), .out30(decoder_1_out0[30]), .out31(decoder_1_out0[31]), .sel(Address_C),
    .en(Write_Enable));
  // NoConnect on Data_In
  // NoConnect on decoder_1_out0[0]
  // NoConnect on Clock
  Register #(.width(32)) x2 (.D(Data_In), .en(decoder_1_out0[2]), .clk(Clock), .Q(x2_q), .clr(Reset));
  Register #(.width(32)) x4 (.D(Data_In), .en(decoder_1_out0[4]), .clk(Clock), .Q(x4_q), .clr(Reset));
  Register #(.width(32)) x6 (.D(Data_In), .en(decoder_1_out0[6]), .clk(Clock), .Q(x6_q), .clr(Reset));
  Register #(.width(32)) x8 (.D(Data_In), .en(decoder_1_out0[8]), .clk(Clock), .Q(x8_q), .clr(Reset));
  Register #(.width(32)) x10 (.D(Data_In), .en(decoder_1_out0[10]), .clk(Clock), .Q(x10_q), .clr(Reset));
  Register #(.width(32)) x12 (.D(Data_In), .en(decoder_1_out0[12]), .clk(Clock), .Q(x12_q), .clr(Reset));
  Register #(.width(32)) x14 (.D(Data_In), .en(decoder_1_out0[14]), .clk(Clock), .Q(x14_q), .clr(Reset));
  Register #(.width(32)) x16 (.D(Data_In), .en(decoder_1_out0[16]), .clk(Clock), .Q(x16_q), .clr(Reset));
  Register #(.width(32)) x18 (.D(Data_In), .en(decoder_1_out0[18]), .clk(Clock), .Q(x18_q), .clr(Reset));
  Register #(.width(32)) x20 (.D(Data_In), .en(decoder_1_out0[20]), .clk(Clock), .Q(x20_q), .clr(Reset));
  Register #(.width(32)) x22 (.D(Data_In), .en(decoder_1_out0[22]), .clk(Clock), .Q(x22_q), .clr(Reset));
  Register #(.width(32)) x24 (.D(Data_In), .en(decoder_1_out0[24]), .clk(Clock), .Q(x24_q), .clr(Reset));
  Register #(.width(32)) x26 (.D(Data_In), .en(decoder_1_out0[26]), .clk(Clock), .Q(x26_q), .clr(Reset));
  Register #(.width(32)) x28 (.D(Data_In), .en(decoder_1_out0[28]), .clk(Clock), .Q(x28_q), .clr(Reset));
  Register #(.width(32)) x30 (.D(Data_In), .en(decoder_1_out0[30]), .clk(Clock), .Q(x30_q), .clr(Reset));
  Register #(.width(32)) x1 (.D(Data_In), .en(decoder_1_out0[1]), .clk(Clock), .Q(x1_q), .clr(Reset));
  Register #(.width(32)) x3 (.D(Data_In), .en(decoder_1_out0[3]), .clk(Clock), .Q(x3_q), .clr(Reset));
  Register #(.width(32)) x5 (.D(Data_In), .en(decoder_1_out0[5]), .clk(Clock), .Q(x5_q), .clr(Reset));
  Register #(.width(32)) x7 (.D(Data_In), .en(decoder_1_out0[7]), .clk(Clock), .Q(x7_q), .clr(Reset));
  Register #(.width(32)) x9 (.D(Data_In), .en(decoder_1_out0[9]), .clk(Clock), .Q(x9_q), .clr(Reset));
  Register #(.width(32)) x11 (.D(Data_In), .en(decoder_1_out0[11]), .clk(Clock), .Q(x11_q), .clr(Reset));
  Register #(.width(32)) x13 (.D(Data_In), .en(decoder_1_out0[13]), .clk(Clock), .Q(x13_q), .clr(Reset));
  Register #(.width(32)) x15 (.D(Data_In), .en(decoder_1_out0[15]), .clk(Clock), .Q(x15_q), .clr(Reset));
  Register #(.width(32)) x17 (.D(Data_In), .en(decoder_1_out0[17]), .clk(Clock), .Q(x17_q), .clr(Reset));
  Register #(.width(32)) x19 (.D(Data_In), .en(decoder_1_out0[19]), .clk(Clock), .Q(x19_q), .clr(Reset));
  Register #(.width(32)) x21 (.D(Data_In), .en(decoder_1_out0[21]), .clk(Clock), .Q(x21_q), .clr(Reset));
  Register #(.width(32)) x23 (.D(Data_In), .en(decoder_1_out0[23]), .clk(Clock), .Q(x23_q), .clr(Reset));
  Register #(.width(32)) x25 (.D(Data_In), .en(decoder_1_out0[25]), .clk(Clock), .Q(x25_q), .clr(Reset));
  Register #(.width(32)) x27 (.D(Data_In), .en(decoder_1_out0[27]), .clk(Clock), .Q(x27_q), .clr(Reset));
  Register #(.width(32)) x29 (.D(Data_In), .en(decoder_1_out0[29]), .clk(Clock), .Q(x29_q), .clr(Reset));
  Register #(.width(32)) x31 (.D(Data_In), .en(decoder_1_out0[31]), .clk(Clock), .Q(x31_q), .clr(Reset));
  Multiplexer #(.disabled("Z"), .enable("true"), .select(5), .width(32)) multiplexer_1 (
    .in0({32{1'b0}}), .in1(x1_q), .in2(x2_q), .in3(x3_q), .in4(x4_q), .in5(x5_q), .in6(x6_q), .in7(x7_q),
    .in8(x8_q), .in9(x9_q), .in10(x10_q), .in11(x11_q), .in12(x12_q), .in13(x13_q), .in14(x14_q),
    .in15(x15_q), .in16(x16_q), .in17(x17_q), .in18(x18_q), .in19(x19_q), .in20(x20_q), .in21(x21_q),
    .in22(x22_q), .in23(x23_q), .in24(x24_q), .in25(x25_q), .in26(x26_q), .in27(x27_q), .in28(x28_q),
    .in29(x29_q), .in30(x30_q), .in31(x31_q), .out(A_Data_Out), .sel(Address_A), .en(Read_Enable));
  Multiplexer #(.disabled("Z"), .enable("true"), .select(5), .width(32)) multiplexer_2 (
    .in0({32{1'b0}}), .in1(x1_q), .in2(x2_q), .in3(x3_q), .in4(x4_q), .in5(x5_q), .in6(x6_q), .in7(x7_q),
    .in8(x8_q), .in9(x9_q), .in10(x10_q), .in11(x11_q), .in12(x12_q), .in13(x13_q), .in14(x14_q),
    .in15(x15_q), .in16(x16_q), .in17(x17_q), .in18(x18_q), .in19(x19_q), .in20(x20_q), .in21(x21_q),
    .in22(x22_q), .in23(x23_q), .in24(x24_q), .in25(x25_q), .in26(x26_q), .in27(x27_q), .in28(x28_q),
    .in29(x29_q), .in30(x30_q), .in31(x31_q), .out(B_Data_Out), .sel(Address_B), .en(Read_Enable));
endmodule

module Operation_Controller (
  input  [31:0] P_Bus_In,
  input  Clock,
  input  Reset,
  input  Phase1n,
  input  Phase2n,
  input  Phase3n,
  input  Phase1s,
  input  Phase2s,
  input  Phase3s,
  input  Phase2i,
  input  Phase3i,
  input  [3:0] CNZV,
  output [31:0] Immediate,
  output [14:0] Register_Adresses,
  output [2:0] Funct3,
  output ALU_Use_PC,
  output Use_Immediate,
  output Alu_Read,
  output Shifter_Read_C,
  output Shifter_Write_L,
  output Shifter_Read_L,
  output Register_File_Write,
  output Load_Upper_Immediate,
  output [4:0] OP_Function,
  output PC_Read_Next,
  output PC_Write_Next,
  output Address_ALU_Use_PC,
  output PC_Jump,
  output PC_Use_Offset,
  output PAD_Read,
  output Data_IO_Store,
  output PAD_Write,
  output Data_IO_Read,
  output Load_Store
);

  wire ALU, and_3_out, and_5_out, and_8_out, and_10_out, and_13_out, Branch, condition_decoder_1_equal,
       condition_decoder_1_greater_or_equal, condition_decoder_1_greater_than_unsigned,
       condition_decoder_1_less, condition_decoder_1_less_unsigned, condition_decoder_1_not_equal,
       Floating_Point, Immediate_t, Jump_PC_Relative, Jump_Register_Relative, Load, Load_Upper_Immediate_t,
       multiplexer_2_out, not_2_out, Operation, or_1_out, or_2_out, or_3_out, or_4_out, or_6_out, or_7_out,
       or_9_out, or_10_out, or_12_out, Shifter, System;
  wire [4:0] multiplexer_3_out;
  wire [4:4] not_1_out;
  wire [6:0] Current_Instruction_q, Funct7;
  wire [31:0] multiplexer_1_out, Next_Instruction_q;

  Multiplexer #(.width(32)) multiplexer_1 (.in0(P_Bus_In), .in1(32'hc80000), .out(multiplexer_1_out), .sel(Phase2i));
  Register #(.width(32)) Next_Instruction (
    .D(multiplexer_1_out), .en(or_1_out), .clk(Clock), .Q(Next_Instruction_q));  // open: clr
  or or_1 (or_1_out, Phase2n, Phase2i);
  Register #(.width(32)) Current_Instruction (
    .D(Next_Instruction_q), .en(Phase1n), .clk(Clock),
    .Q({Funct7, Register_Adresses[14:5], Funct3, Register_Adresses[4:0], Current_Instruction_q}), .clr(Reset));
  // Probe on Current_Instruction_q
  or or_2 (or_2_out, ALU_Use_PC, Load_Upper_Immediate_t);
  Operation_Decoder operation_decoder_1 (
    .OPCODE(Current_Instruction_q), .FLOATING_POINT(Floating_Point), .IMMEDIATE(Immediate_t), .LOAD(Load),
    .OPERATION(Operation), .ADD_UPPER_IMMEDIATE_PC(ALU_Use_PC), .STORE(PC_Use_Offset),
    .LOAD_UPPER_IMMEDIATE(Load_Upper_Immediate_t), .BRANCH(Branch),
    .JUMP_AND_LINK_REGISTER(Jump_Register_Relative), .JUMP_AND_LINK(Jump_PC_Relative), .SYSTEM(System));
  Immediate_Decoder immediate_decoder_1 (
    .Instruction({Funct7, Register_Adresses[14:5], Funct3, Register_Adresses[4:0], Current_Instruction_q}),
    .Immediate_Instruction(Immediate_t), .Store(PC_Use_Offset), .Branch(Branch), .Upper_Immediate(or_2_out),
    .Jump(Jump_PC_Relative), .Immediate(Immediate));
  Condition_Decoder condition_decoder_1 (
    .Carry_In(CNZV[0]), .Negative(CNZV[1]), .Zero(CNZV[2]), .Overflow(CNZV[3]),
    .Not_Equal(condition_decoder_1_not_equal), .Equal(condition_decoder_1_equal),
    .Less(condition_decoder_1_less), .Greater_Or_Equal(condition_decoder_1_greater_or_equal),
    .Greater_Than_Unsigned(condition_decoder_1_greater_than_unsigned),
    .Less_Unsigned(condition_decoder_1_less_unsigned));
  Multiplexer #(.select(3)) multiplexer_2 (
    .in0(condition_decoder_1_equal), .in1(condition_decoder_1_not_equal), .in4(condition_decoder_1_less),
    .in5(condition_decoder_1_greater_or_equal), .in6(condition_decoder_1_less_unsigned),
    .in7(condition_decoder_1_greater_than_unsigned), .out(multiplexer_2_out), .sel(Funct3));  // open: in2, in3
  or or_3 (or_3_out, Load_Upper_Immediate_t, ALU_Use_PC, Operation, Load, Jump_PC_Relative, Jump_Register_Relative, System);
  and and_1 (Register_File_Write, Phase3n, or_3_out);
  or or_4 (or_4_out, Jump_Register_Relative, Jump_PC_Relative);
  and and_2 (PC_Read_Next, or_4_out, Phase3n);
  or or_5 (PC_Write_Next, Phase3i, Phase3n);
  and and_3 (and_3_out, Branch, multiplexer_2_out);
  or or_6 (or_6_out, and_3_out, Jump_Register_Relative, Jump_PC_Relative);
  and and_4 (PC_Jump, or_6_out, Phase3n);
  not not_1 (not_1_out[4], Funct3[2]);
  or or_7 (or_7_out, Branch, ALU_Use_PC, ALU);
  and and_5 (and_5_out, Phase3n, or_7_out);
  Multiplexer #(.width(5)) multiplexer_3 (
    .in0({not_1_out[4], 4'b0101}), .in1(5'b10000), .out(multiplexer_3_out), .sel(Branch));
  or or_8 (Alu_Read, and_5_out, and_8_out);
  Multiplexer #(.width(5)) multiplexer_4 (
    .in0(multiplexer_3_out), .in1({Funct7[5], Funct7[1], Funct3}), .out(OP_Function), .sel(Operation));
  and and_6 (Data_IO_Store, Phase2s, PC_Use_Offset);
  and and_7 (Data_IO_Read, Phase2s, Load);
  or or_9 (or_9_out, PC_Use_Offset, Load);
  and and_8 (and_8_out, Phase3s, or_9_out);
  or or_10 (or_10_out, OP_Function[2], ~OP_Function[4]);  // OR_Gate
  or or_11 (Address_ALU_Use_PC, Branch, Jump_PC_Relative);
  or or_12 (or_12_out, Shifter, Load);
  and and_9 (Shifter_Read_C, Phase3n, or_12_out);
  and and_10 (and_10_out, OP_Function[0], ~OP_Function[1], ~OP_Function[3], or_10_out);  // AND_Gate
  not not_2 (not_2_out, and_10_out);
  and and_11 (Shifter, and_10_out, Operation);
  and and_12 (ALU, not_2_out, Operation);
  and and_13 (and_13_out, Load, Phase1s);
  and and_14 (PAD_Write, Phase2s, PC_Use_Offset);
  or or_13 (Load_Store, PC_Use_Offset, Load);
  and and_15 (Shifter_Write_L, Phase2s, Load);
  or or_14 (PAD_Read, Phase2n, and_13_out);
  and and_16 (Shifter_Read_L, Phase2s, PC_Use_Offset);
  and and_17 (Load_Upper_Immediate, Load_Upper_Immediate_t, Phase3n);
  or or_15 (Use_Immediate, ALU_Use_PC, Immediate_t);

  // Other names for the same wires on the sheet: Funct10[9:0] = {Funct7, Funct3}; Add_Upper_Immediate_PC = ALU_Use_PC;
  //   Store = PC_Use_Offset

  // Notes on the sheet:
  //   Calli 25:
  //   Register File
  //   Program Counter
  //   Input/Output and interface Pads
  //   ALU And Shifter
endmodule

module Operation_Decoder (
  input  [6:0] OPCODE,
  output FLOATING_POINT,
  output IMMEDIATE,
  output LOAD,
  output OPERATION,
  output ADD_UPPER_IMMEDIATE_PC,
  output STORE,
  output LOAD_UPPER_IMMEDIATE,
  output BRANCH,
  output JUMP_AND_LINK_REGISTER,
  output JUMP_AND_LINK,
  output SYSTEM
);

  wire not_1_out, not_2_out, not_3_out, not_4_out, not_5_out, or_1_out, or_2_out, or_3_out, or_4_out;

  not not_1 (not_1_out, OPCODE[6]);
  not not_2 (not_2_out, OPCODE[5]);
  not not_3 (not_3_out, OPCODE[4]);
  not not_4 (not_4_out, OPCODE[3]);
  not not_5 (not_5_out, OPCODE[2]);
  or or_1 (or_1_out, OPCODE[6], not_3_out);
  or or_2 (or_2_out, not_1_out, not_2_out);
  or or_3 (or_3_out, OPCODE[4], OPCODE[2]);
  and and_1 (IMMEDIATE, not_2_out, not_1_out, not_5_out);
  and and_2 (LOAD, not_3_out, not_2_out);
  or or_4 (or_4_out, not_1_out, not_2_out);
  and and_3 (ADD_UPPER_IMMEDIATE_PC, OPCODE[2], OPCODE[4], not_2_out);
  and and_4 (STORE, OPCODE[5], not_3_out, not_1_out);
  and and_5 (LOAD_UPPER_IMMEDIATE, OPCODE[2], OPCODE[5], OPCODE[4]);
  and and_6 (BRANCH, OPCODE[6], not_3_out, not_5_out);
  and and_7 (JUMP_AND_LINK_REGISTER, OPCODE[2], not_4_out, OPCODE[6]);
  and and_8 (JUMP_AND_LINK, OPCODE[3], OPCODE[6]);
  and and_9 (SYSTEM, OPCODE[6], OPCODE[5], OPCODE[4]);
  and and_10 (FLOATING_POINT, or_1_out, or_2_out, or_3_out);
  and and_11 (OPERATION, OPCODE[4], or_4_out, not_5_out);
endmodule

module Condition_Decoder (
  input  Carry_In,
  input  Negative,
  input  Zero,
  input  Overflow,
  output Not_Equal,
  output Equal,
  output Less,
  output Greater_Or_Equal,
  output Greater_Than_Unsigned,
  output Less_Unsigned
);

  not not_1 (Not_Equal, Zero);
  xor xor_1 (Less, Overflow, Negative);
  not not_2 (Greater_Or_Equal, Less);
  not not_3 (Greater_Than_Unsigned, Carry_In);

  assign Equal = Zero;
  assign Less_Unsigned = Carry_In;
endmodule

module Byte_Decoder (
  input  [1:0] Data_Size,
  input  [1:0] Data_Offset,
  output [2:0] Mux_Enables
);

  wire and_1_out, and_2_out, and_3_out;

  and and_1 (and_1_out, Data_Offset[1], Data_Offset[0]);
  and and_2 (and_2_out, Data_Size[0], Data_Offset[1]);
  and and_3 (and_3_out, Data_Size[0], Data_Offset[0]);
  or or_1 (Mux_Enables[0], Data_Offset[0], Data_Offset[1], Data_Size[0], Data_Size[1]);
  or or_2 (Mux_Enables[2], and_1_out, and_2_out, Data_Size[1]);
  or or_3 (Mux_Enables[1], Data_Offset[1], and_3_out, Data_Size[1]);
endmodule

module IO_Controller (
  input  [1:0] Data_Size,
  input  [31:0] Keyboard_Address,
  input  [31:0] Video_Address,
  input  [31:0] Address_In,
  input  Phase1n,
  input  Phase3s,
  input  Phase3i,
  input  Reset,
  input  Clock,
  input  Read,
  input  Write,
  output Data_2Bytes,
  output Data_4Bytes,
  output [31:0] AddressDebug,
  output Read_Keyboard,
  output Write_Video,
  output [23:0] Address_Out_24Bit,
  output ReadRam,
  output Read_OS_Ram,
  output [7:0] Rom_Address_Out_8Bit,
  output WriteRam,
  output Write_OS_Ram
);

  wire comparator_1_eq, comparator_2_eq, decoder_1_out0, decoder_1_out1, decoder_2_out0, decoder_2_out1,
       decoder_2_out2, or_1_out;
  wire [31:24] Memory_Address_q;

  Register #(.width(32)) Memory_Address (
    .D(Address_In), .en(or_1_out), .clk(Clock), .Q({Memory_Address_q, Address_Out_24Bit}), .clr(Reset));
  or or_1 (or_1_out, Phase1n, Phase3s, Phase3i);
  Comparator #(.width(32)) comparator_1 (
    .a(Keyboard_Address), .b({Memory_Address_q, Address_Out_24Bit}), .eq(comparator_1_eq));  // open: gt, lt
  Comparator #(.width(32)) comparator_2 (
    .a(Video_Address), .b({Memory_Address_q, Address_Out_24Bit}), .eq(comparator_2_eq));  // open: gt, lt
  Decoder #(.select(2)) decoder_1 (
    .out0(decoder_1_out0), .out1(decoder_1_out1), .out3(Write_OS_Ram), .sel(Memory_Address_q[31:30]),
    .en(Write));  // open: out2
  and and_1 (Read_Keyboard, comparator_1_eq, Read);
  and and_2 (Write_Video, comparator_2_eq, Write);
  or or_2 (WriteRam, decoder_1_out0, decoder_1_out1);
  or or_3 (Data_2Bytes, Data_Size[0], Data_Size[1]);
  Decoder #(.select(2)) decoder_2 (
    .out0(decoder_2_out0), .out1(decoder_2_out1), .out2(decoder_2_out2), .out3(Read_OS_Ram),
    .sel(Memory_Address_q[31:30]), .en(Read));
  or or_4 (ReadRam, decoder_2_out0, decoder_2_out1);
  assign Rom_Address_Out_8Bit = decoder_2_out2 ? Address_Out_24Bit[9:2] : 8'bz;  // Controlled_Buffer controlled_buffer_1

  assign Data_4Bytes = Data_Size[1];
endmodule

module Immediate_Decoder (
  input  Immediate_Instruction,
  input  [31:0] Instruction,
  input  Store,
  input  Branch,
  input  Upper_Immediate,
  input  Jump,
  output [31:0] Immediate
);

  wire [31:0] bit_extender_1_out, bit_extender_2_out, bit_extender_3_out, bit_extender_4_out;

  assign bit_extender_1_out = {{20{Instruction[31]}}, Instruction[31:20]};  // Bit_Extender bit_extender_1
  assign bit_extender_2_out = {{20{Instruction[31]}}, {Instruction[31:25], Instruction[11:7]}};  // Bit_Extender bit_extender_2
  assign bit_extender_3_out = {{19{Instruction[31]}}, {Instruction[31], Instruction[7], Instruction[30:25], Instruction[11:8], 1'b0}};  // Bit_Extender bit_extender_3
  assign bit_extender_4_out = {{11{Instruction[31]}}, {Instruction[31], Instruction[19:12], Instruction[20], Instruction[30:21], 1'b0}};  // Bit_Extender bit_extender_4
  assign Immediate = Immediate_Instruction ? bit_extender_1_out : 32'bz;  // Controlled_Buffer controlled_buffer_1
  assign Immediate = Store ? bit_extender_2_out : 32'bz;  // Controlled_Buffer controlled_buffer_2
  assign Immediate = Branch ? bit_extender_3_out : 32'bz;  // Controlled_Buffer controlled_buffer_3
  assign Immediate = Upper_Immediate ? {Instruction[31:12], {12{1'b0}}} : 32'bz;  // Controlled_Buffer controlled_buffer_4
  assign Immediate = Jump ? bit_extender_4_out : 32'bz;  // Controlled_Buffer controlled_buffer_5

  // Notes on the sheet:
  //   I-type
  //   S-type
  //   B-type
  //   U-type
  //   J-type
endmodule

module Address_ALU (
  input  Calculate,
  input  Write,
  input  Use_PC,
  input  [31:0] Source1,
  input  [31:0] Program_Counter_In,
  input  [31:0] Immediate,
  input  Clock,
  output [31:0] Result
);

  wire not_1_out;
  wire [31:0] adder_1_out, multiplexer_1_out, Source_1_q, Source_2_q;

  not not_1 (not_1_out, Clock);
  Multiplexer #(.width(32)) multiplexer_1 (
    .in0(Source1), .in1(Program_Counter_In), .out(multiplexer_1_out), .sel(Use_PC));
  Register #(.width(32)) Source_1 (.D(multiplexer_1_out), .en(Write), .clk(not_1_out), .Q(Source_1_q));  // open: clr
  Register #(.width(32)) Source_2 (.D(Immediate), .en(Write), .clk(not_1_out), .Q(Source_2_q));  // open: clr
  Adder #(.width(32)) adder_1 (.a(Source_1_q), .b(Source_2_q), .out(adder_1_out));  // open: cin, cout
  Register #(.width(32)) Result_Reg (.D(adder_1_out), .en(Calculate), .clk(not_1_out), .Q(Result));  // open: clr

  // Notes on the sheet:
  //   Source1: initial=0xffffffff
endmodule

module Register_History_Generator (
  input  [31:0] Current_Value,
  input  [4:0] Current_Address,
  input  [4:0] Target_Address,
  input  Write_Signal,
  input  Reset,
  input  Clock,
  output Out_Clock,
  output [15:0] Out_Value
);

  wire and_1_out, comparator_1_eq, comparator_2_gt;
  wire [3:0] counter_1_q;
  wire [31:0] Last_Value_q;

  Comparator #(.width(5)) comparator_1 (.a(Current_Address), .b(Target_Address), .eq(comparator_1_eq));  // open: gt, lt
  and and_1 (and_1_out, comparator_1_eq, Write_Signal);
  Register #(.trigger("falling"), .width(32)) Last_Value (
    .D(Current_Value), .en(and_1_out), .clk(Clock), .Q(Last_Value_q), .clr(Reset));
  and and_2 (Out_Clock, and_1_out, Clock);
  Comparator #(.width(32)) comparator_2 (.a(Current_Value), .b(Last_Value_q), .gt(comparator_2_gt));  // open: eq, lt
  Counter #(.max('hf), .width(4)) counter_1 (
    .clr(Reset), .up(comparator_2_gt), .count(and_1_out), .clk(Clock), .Q(counter_1_q));  // open: load, D, carry
  Decoder #(.enable("false"), .select(4)) decoder_1 (
    .out0(Out_Value[0]), .out1(Out_Value[1]), .out2(Out_Value[2]), .out3(Out_Value[3]), .out4(Out_Value[4]),
    .out5(Out_Value[5]), .out6(Out_Value[6]), .out7(Out_Value[7]), .out8(Out_Value[8]), .out9(Out_Value[9]),
    .out10(Out_Value[10]), .out11(Out_Value[11]), .out12(Out_Value[12]), .out13(Out_Value[13]),
    .out14(Out_Value[14]), .out15(Out_Value[15]), .sel(counter_1_q));
endmodule
